# Fritzing sketch kapcs_rajz (saved by Fritzing 0.9.9b)
breadboards: 1

parts:
  R1 = Resistor [tolerance=±5% power=0.25 resistance=220 package=THT]
  R2 = Resistor [tolerance=±5% power=0.25 resistance=220 package=THT]
  R3 = Resistor [tolerance=±5% power=0.25 resistance=220 package=THT]
  R4 = Resistor [tolerance=±5% power=0.25 resistance=220 package=THT]
  R5 = Resistor [tolerance=±5% power=0.25 resistance=220 package=THT]
  R6 = Resistor [tolerance=±5% power=0.25 resistance=220 package=THT]
  LCD1 = LCD screen
  SP1 = SPEAKER [package=pcb_mount_speaker]
  M1 = DC Motor
  IC1 = L293D [package=THT]
  LED1 = RGB LED - (4 legs) [package="5 mm [THT]"]
  Part3 = RFID-RC522-v2
  Part4 = Arduino Pro Micro (Clone)

nets:
  N1: R1.Pin_0, LED1.common_anode
  N2: R1.Pin_1, Part4.A3
  N3: R2.Pin_0, LED1.blue_cathode
  N4: R2.Pin_1, Part4.A1
  N5: R3.Pin_0, LED1.red_cathode
  N6: R3.Pin_1, Part4.A2
  N7: R4.Pin_0, R5.Pin_0, Part3.3.3V
  N8: R4.Pin_1, R6.Pin_0
  GND: R5.Pin_1, LCD1.VSS, SP1.+, IC1.0V, Part3.GND, Part4.GND
  VDD: R6.Pin_1, LCD1.VDD, IC1.Enable_1, IC1.+Vmotor, LED1.green_cathode, Part4.VCC
  N9: LCD1.V0, Part4.D2
  N10: LCD1.RS, Part4.D3
  N11: SP1.-, Part4.D5
  N12: M1.pin_1, IC1.Out_4_(_Controlled_by_Enable_2_)
  N13: M1.pin_2, IC1.Out_3_(_Controlled_by_Enable_2_)
  N14: IC1.In_1, Part4.D6
  N15: IC1.In_3, Part4.D7
  N16: Part3.SDA, Part4.D10
  N17: Part3.SCK, Part4.D15
  N18: Part3.MOSI, Part4.D16
  N19: Part3.MISO, Part4.D14
  N20: Part3.RST, Part4.D9

custom parts:
  RFID-RC522-v2: A simple China made RFID-RC522 Reader; do check the pin labels, as this is a MFRC522 based clone.

// code stored in the sketch: sketch_may05a.ino
#include <Wire.h> 
#include <LiquidCrystal_I2C.h>

// Set the LCD address to 0x27 for a 16 chars and 2 line display
LiquidCrystal_I2C lcd(0x27, 16, 2);
char ch;
int red_light_pin= 19;
int green_light_pin = 20;
int blue_light_pin = 21;

int speaker_pin = 5;
String code = "";
String code1 = "open";
String code2 = "closed";
int delay_unit = 250;


int motorPin1 = 7;
int motorPin2 = 8;

#include <SPI.h>
#include <MFRC522.h>
 
#define SS_PIN 10
#define RST_PIN 9
MFRC522 mfrc522(SS_PIN, RST_PIN);

void point(){
  digitalWrite(speaker_pin, HIGH);
  delay(333);
  digitalWrite(speaker_pin, LOW);
  delay(333);
  }

void line(){
digitalWrite(speaker_pin, HIGH);
delay(1000);
digitalWrite(speaker_pin, LOW);
delay(1000);
  
  }

void setup() {

  pinMode(motorPin1, OUTPUT);
  pinMode(motorPin2, OUTPUT);
  
  lcd.begin();
  Serial.begin(9600);
  delay(5000);// Initiate a serial communication
  SPI.begin();// Initiate  SPI bus
  
  lcd.backlight();
  mfrc522.PCD_Init();   // Initiate MFRC522
  
  pinMode(red_light_pin, OUTPUT);
  pinMode(green_light_pin, OUTPUT);
  pinMode(blue_light_pin, OUTPUT);

  

  pinMode(speaker_pin, OUTPUT);
  lcd.println("Approximate your card to the reader...");
  

}
void loop() {

  

  

  
  
  
  RGB_color(0,255,255); // Red
  

  // Look for new cards
  if ( ! mfrc522.PICC_IsNewCardPresent()) 
  {
    return;
  }
  // Select one of the cards
  if ( ! mfrc522.PICC_ReadCardSerial()) 
  {
    return;
  }
  //Show UID on serial monitor
  Serial.print("UID tag :");
  String content= "";
  byte letter;
  for (byte i = 0; i < mfrc522.uid.size; i++) 
  {
     Serial.print(mfrc522.uid.uidByte[i] < 0x10 ? " 0" : " ");
     Serial.print(mfrc522.uid.uidByte[i], HEX);
     content.concat(String(mfrc522.uid.uidByte[i] < 0x10 ? " 0" : " "));
     content.concat(String(mfrc522.uid.uidByte[i], HEX));
  }
  Serial.println();
  content.toUpperCase();
  if (content.substring(1) == "C3 8A 1B 24" || "47 2B 37 53" ) //change here the UID of the card/cards that you want to give access
  {
    lcd.println("Authorized access");
    RGB_color(173,255,47); // Green
    digitalWrite(motorPin1, HIGH);
    /*digitalWrite(speaker_pin, HIGH);
    delay(3000);
    digitalWrite(speaker_pin, LOW);*/
    
    //o
    line();
    delay(100);
    line();
    delay(100);
    line();
    delay(100 * 4);
    //p
    point();
    delay(100);
    line();
    delay(100);
    line();
    delay(100);
    point();
    delay(100 * 4);
    //e
    point();
    delay(100 * 4);
    //n
    line();
    delay(100);
    point();
    delay(100 * 4);
    digitalWrite(motorPin1, LOW);
  }
 
 else   {
    lcd.println(" Access denied");
    RGB_color(0,255,255); 
    delay(3000);
  }

  
  
}
void RGB_color(int red_light_value, int green_light_value, int blue_light_value)
 {
  analogWrite(red_light_pin, red_light_value);
  analogWrite(green_light_pin, green_light_value);
  analogWrite(blue_light_pin, blue_light_value);
}






void morse(){
  if(ch == 'c'){
    c();
  }
  else if(ch == 'l'){
    l();
  }
  else if(ch == 'o'){
    o();
  }
  else if(ch == 's'){
    s();
  }
  else if(ch == 'e'){
    e();
  }
  else if(ch == 'd'){
    d();
  }
  else if(ch == 'p'){
    p();
  }
  else if(ch == 'n'){
    n();
  }
  
}

void String2Morse(){
 int len = code.length();
  for (int i = 0; i < len; i++){
    ch = code.charAt(i);
    morse();
  }
}



void c(){
  line();
  delay(delay_unit);
  point();
  delay(delay_unit);
  line();
  delay(delay_unit);
  point();
  delay(delay_unit * 5);
}

void d(){
  line();
  delay(delay_unit);
  point();
  delay(delay_unit);
  point();
  delay(delay_unit * 5);
}

void e(){
  point();
  delay(delay_unit * 5);
}

void l(){
  point();
  delay(delay_unit);
  line();
  delay(delay_unit);
  point();
  delay(delay_unit);
  point();
  delay(delay_unit * 5);
}

void n(){
  line();
  delay(delay_unit);
  point();
  delay(delay_unit * 5);
}

void o(){
  line();
  delay(delay_unit);
  line();
  delay(delay_unit);
  line();
  delay(delay_unit * 5);
}

void p(){
  point();
  delay(delay_unit);
  line();
  delay(delay_unit);
  line();
  delay(delay_unit);
  point();
  delay(delay_unit * 5);
}

void s(){
  point();
  delay(delay_unit);
  point();
  delay(delay_unit);
  point();
  delay(delay_unit * 5);
}
